# Fritzing sketch alkis lamba cizim (saved by Fritzing 0.9.3b)
breadboards: 1

parts:
  Part3 = Lilypad Battery Connect
  KY-3 = Keyes Relay [package=THT]
  LED3 = LEDs [package=led10mm]
  Parça4 = Arduino Uno (Rev3)
  FC-2 = Sound Sensor

nets:
  N1: Part3.-, LED3.C
  N2: Part3.+, KY-3.C
  5V: KY-3.signal, Parça4.5V, FC-2.VCC
  GND: KY-3.power, Parça4.GND, FC-2.GND
  N3: KY-3.ground, Parça4.D2
  N4: KY-3.NC, LED3.A
  N5: Parça4.D4, FC-2.OUT

notes:
  VCC 5v
  IN > D2
  220V DC power supply
  GND

custom parts:
  Keyes Relay: The Keyes 5V relay module is suitable for SCM development, home appliance control. It uses a 5V~12V TIL control signal which can control DC / AC signal.
  LEDs: LEDs Standard schematic elements and footprints for 5mm, 3mm, 1206, and 0603 sized LEDs. 5mm - Spark Fun Electronics SKU : COM-00529 (and others)
